// Logisim project Project-1.circ as structural Verilog: 13 circuits, main circuit main
module main (
  input  [3:0] Number_B,
  input  [3:0] Number_A,
  input  [3:0] Operation_code,
  output Zero_flag,
  output [3:0] Output,
  output Carry___Borrow,
  output Overflow_flag
);

  wire _1_s_zero_flag, _2_s_overflow, adder_1_carry, adder_1_overflow, and_2_out, multiplication_1_overflow,
       nor_1_out, not_1_out, not_2_out, subtracter_1_borrow, subtracter_1_overflow, subtracter_2_borrow,
       subtracter_2_overflow;
  wire [3:0] _1_s_out_2, _2_s_out_2, adder_1_output, AND_out, Left_arithmetic_out_2, Left_circular_out_2,
       Left_Logic_output, multiplication_1_output, NAND_out, OR_out, Right_Arithmetic_out_2,
       Right_circular_out_2, Right_Logic_out_2, subtracter_1_output, subtracter_2_output, XOR_out;

  Multiplication multiplication_1 (
    .B(Number_B), .A(Number_A), .Overflow(multiplication_1_overflow), .\output (multiplication_1_output));
  assign XOR_out = Number_A ^ Number_B;  // XOR_Gate XOR, 4 bits wide
  _2_s _2_s (.in_1(Number_A), .out_2(_2_s_out_2), .Overflow(_2_s_overflow));
  _1_s _1_s (.in_1(Number_A), .out_2(_1_s_out_2), .Zero_flag(_1_s_zero_flag));
  Left_logic_shift Left_Logic (.A(Number_A), .Output(Left_Logic_output));
  Right_logic_shift Right_Logic (.A(Number_A), .out_2(Right_Logic_out_2));
  Left_Arithmetic Left_arithmetic (.in_1(Number_A), .out_2(Left_arithmetic_out_2));
  Right_Arithmetic Right_Arithmetic (.A(Number_A), .out_2(Right_Arithmetic_out_2));
  left_circular Left_circular (.A(Number_A), .out_2(Left_circular_out_2));
  right_circular_shift Right_circular (.A(Number_A), .out_2(Right_circular_out_2));
  adder adder_1 (
    .A(Number_A), .B(Number_B), .overflow(adder_1_overflow), .Output(adder_1_output), .carry(adder_1_carry));
  subtracter subtracter_1 (
    .A(Number_B), .B(Number_A), .overflow(subtracter_1_overflow), .Output(subtracter_1_output),
    .Borrow(subtracter_1_borrow));
  assign NAND_out = ~(Number_A & Number_B);  // NAND_Gate NAND, 4 bits wide
  subtracter subtracter_2 (
    .A(Number_A), .B(Number_B), .overflow(subtracter_2_overflow), .Output(subtracter_2_output),
    .Borrow(subtracter_2_borrow));
  assign AND_out = Number_A & Number_B;  // AND_Gate AND, 4 bits wide
  assign OR_out = Number_A | Number_B;  // OR_Gate OR, 4 bits wide
  Multiplexer #(.select(4), .width(4), .enable("false")) multiplexer_1 (
    .in0(adder_1_output), .in1(subtracter_2_output), .in2(subtracter_1_output),
    .in3(multiplication_1_output), .in4(AND_out), .in5(OR_out), .in6(XOR_out), .in7(NAND_out),
    .in8(_2_s_out_2), .in9(_1_s_out_2), .in10(Left_Logic_output), .in11(Right_Logic_out_2),
    .in12(Left_arithmetic_out_2), .in13(Right_Arithmetic_out_2), .in14(Left_circular_out_2),
    .in15(Right_circular_out_2), .out(Output), .sel(Operation_code));
  Multiplexer #(.select(4), .enable("false")) multiplexer_2 (
    .in0(adder_1_carry), .in1(subtracter_2_borrow), .in2(subtracter_1_borrow), .in3(1'b0), .in4(1'b0),
    .in5(1'b0), .in6(1'b0), .in7(1'b0), .in8(1'b0), .in9(1'b0), .in10(1'b0), .in11(1'b0), .in12(1'b0),
    .in13(1'b0), .in14(1'b0), .in15(1'b0), .out(Carry___Borrow), .sel(Operation_code));
  Multiplexer #(.select(4), .enable("false")) multiplexer_3 (
    .in0(adder_1_overflow), .in1(subtracter_2_overflow), .in2(subtracter_1_overflow),
    .in3(multiplication_1_overflow), .in4(1'b0), .in5(1'b0), .in6(1'b0), .in7(1'b0), .in8(_2_s_overflow),
    .in9(1'b0), .in10(1'b0), .in11(1'b0), .in12(1'b0), .in13(1'b0), .in14(1'b0), .in15(1'b0),
    .out(Overflow_flag), .sel(Operation_code));
  nor nor_1 (nor_1_out, Output[0], Output[1], Output[2], Output[3]);
  or or_2 (Zero_flag, nor_1_out, and_2_out);
  not not_1 (not_1_out, Operation_code[1]);
  not not_2 (not_2_out, Operation_code[2]);
  and and_2 (and_2_out, Operation_code[0], not_1_out, not_2_out, Operation_code[3], _1_s_zero_flag);

  // Notes on the sheet:
  //   Main multiplexer
  //   Operation code
  //   Carry/Borrow
  //   Overflow
endmodule

module Presenting (
  input  [3:0] A,
  input  [3:0] B,
  input  [3:0] Code,
  output Zero_flag,
  output [3:0] Output,
  output Carry_Borrow,
  output Overflow
);

  main main_1 (
    .Number_B(B), .Number_A(A), .Operation_code(Code), .Zero_flag(Zero_flag), .Output(Output),
    .Carry___Borrow(Carry_Borrow), .Overflow_flag(Overflow));
endmodule

// Add
module adder (
  input  [3:0] A,
  input  [3:0] B,
  output overflow,
  output [3:0] Output,
  output carry
);

  wire and_1_out, and_2_out, not_1_out, not_2_out, not_3_out;

  Adder #(.width(4)) adder_1 (.a(A), .b(B), .out(Output), .cout(carry));  // open: cin
  and and_1 (and_1_out, A[3], B[3], not_1_out);
  not not_1 (not_1_out, Output[3]);
  not not_2 (not_2_out, A[3]);
  not not_3 (not_3_out, B[3]);
  and and_2 (and_2_out, not_2_out, not_3_out, Output[3]);
  or or_1 (overflow, and_1_out, and_2_out);
endmodule

// Sub
module subtracter (
  input  [3:0] A,
  input  [3:0] B,
  output overflow,
  output [3:0] Output,
  output Borrow
);

  wire and_1_out, and_2_out, not_1_out, not_2_out, not_3_out;

  Subtractor #(.width(4)) subtractor_1 (.a(A), .b(B), .out(Output), .bout(Borrow));  // open: bin
  not not_1 (not_1_out, A[3]);
  and and_1 (and_1_out, not_1_out, B[3], Output[3]);
  not not_2 (not_2_out, B[3]);
  not not_3 (not_3_out, Output[3]);
  and and_2 (and_2_out, A[3], not_2_out, not_3_out);
  or or_1 (overflow, and_1_out, and_2_out);
endmodule

module Left_logic_shift (
  input  [3:0] A,
  output [3:0] Output
);


  assign Output = {A[2:0], 1'b0};

  // Notes on the sheet:
  //   A
  //   left logical shift
  //   A0
  //   A1
  //   A2
endmodule

module Right_logic_shift (
  input  [3:0] A,
  output [3:0] out_2
);


  assign out_2 = {1'b0, A[3:1]};

  // Notes on the sheet:
  //   right logical shift
endmodule

module right_circular_shift (
  input  [3:0] A,
  output [3:0] out_2
);


  assign out_2 = {A[0], A[3:1]};
endmodule

module left_circular (
  input  [3:0] A,
  output [3:0] out_2
);


  assign out_2 = {A[2:0], A[3]};
endmodule

module Left_Arithmetic (
  input  [3:0] in_1,
  output [3:0] out_2
);


  assign out_2 = {in_1[2:0], 1'b0};
endmodule

module Right_Arithmetic (
  input  [3:0] A,
  output [3:0] out_2
);


  assign out_2 = {{2{A[3]}}, A[2:1]};
endmodule

module _2_s (
  input  [3:0] in_1,
  output [3:0] out_2,
  output Overflow
);

  wire and_1_out, and_2_out, and_4_out, not_1_out, not_2_out, not_3_out, not_4_out;

  not not_1 (not_1_out, in_1[0]);
  not not_2 (not_2_out, in_1[1]);
  not not_3 (not_3_out, in_1[2]);
  not not_4 (not_4_out, in_1[3]);
  and and_1 (and_1_out, 1'b1, not_1_out);
  xor xor_1 (out_2[0], 1'b1, not_1_out);
  and and_2 (and_2_out, and_1_out, not_2_out);
  and and_3 (Overflow, not_1_out, not_2_out, not_3_out, in_1[3]);
  xor xor_2 (out_2[1], and_1_out, not_2_out);
  xor xor_3 (out_2[2], and_2_out, not_3_out);
  and and_4 (and_4_out, not_3_out, and_2_out);
  xor xor_4 (out_2[3], and_4_out, not_4_out);

  // Notes on the sheet:
  //   2's complement
endmodule

module _1_s (
  input  [3:0] in_1,
  output [3:0] out_2,
  output Zero_flag
);

  wire and_1_out, and_2_out;

  not not_1 (out_2[0], in_1[0]);
  not not_2 (out_2[1], in_1[1]);
  not not_3 (out_2[2], in_1[2]);
  not not_4 (out_2[3], in_1[3]);
  and and_1 (and_1_out, in_1[0], in_1[1], in_1[2], in_1[3]);
  and and_2 (and_2_out, out_2[0], out_2[1], out_2[2], out_2[3]);
  or or_1 (Zero_flag, and_2_out, and_1_out);

  // Notes on the sheet:
  //   Zero
  //   1's complement
endmodule

module Multiplication (
  input  [3:0] B,
  input  [3:0] A,
  output Overflow,
  output [3:0] \output 
);

  wire adder_2_cout, adder_3_cout, adder_3_out, adder_4_cout, adder_5_cout, adder_5_out, adder_6_cout,
       adder_6_out, adder_7_cout, adder_8_cout, adder_8_out, adder_9_cout, adder_9_out, adder_10_cout,
       adder_11_cout, adder_11_out, adder_12_cout, adder_13_cout, and_1_out, and_2_out, and_3_out, and_4_out,
       and_5_out, and_6_out, and_7_out, and_8_out, and_9_out, nand_1_out, nand_2_out, nand_3_out, nand_4_out,
       nand_5_out, nand_6_out, nand_7_out, nand_8_out, not_1_out, not_2_out, not_3_out, not_4_out, not_5_out;
  wire [7:4] adder_7_out;

  Adder #(.width(1)) adder_1 (.a(1'b0), .b(1'b1), .out(adder_7_out[7]), .cin(adder_2_cout));  // open: cout
  and and_1 (and_1_out, A[3], B[3]);
  Adder #(.width(1)) adder_2 (
    .a(and_1_out), .b(adder_3_cout), .out(adder_7_out[6]), .cin(adder_4_cout), .cout(adder_2_cout));
  nand nand_1 (nand_1_out, A[3], B[2]);
  Adder #(.width(1)) adder_3 (
    .a(nand_1_out), .b(adder_5_cout), .out(adder_3_out), .cin(adder_6_cout), .cout(adder_3_cout));
  nand nand_2 (nand_2_out, A[2], B[3]);
  Adder #(.width(1)) adder_4 (
    .a(nand_2_out), .b(adder_3_out), .out(adder_7_out[5]), .cin(adder_7_cout), .cout(adder_4_cout));
  nand nand_3 (nand_3_out, A[3], B[1]);
  Adder #(.width(1)) adder_5 (.a(nand_3_out), .b(1'b1), .out(adder_5_out), .cin(adder_8_cout), .cout(adder_5_cout));
  and and_2 (and_2_out, A[2], B[2]);
  nand nand_4 (nand_4_out, A[1], B[3]);
  Adder #(.width(1)) adder_6 (
    .a(and_2_out), .b(adder_5_out), .out(adder_6_out), .cin(adder_9_cout), .cout(adder_6_cout));
  Adder #(.width(1)) adder_7 (
    .a(nand_4_out), .b(adder_6_out), .out(adder_7_out[4]), .cin(adder_10_cout), .cout(adder_7_cout));
  nand nand_5 (nand_5_out, A[3], B[0]);
  and and_3 (and_3_out, A[2], B[1]);
  Adder #(.width(1)) adder_8 (
    .a(and_3_out), .b(nand_5_out), .out(adder_8_out), .cin(adder_11_cout), .cout(adder_8_cout));
  and and_4 (and_4_out, A[1], B[2]);
  Adder #(.width(1)) adder_9 (
    .a(and_4_out), .b(adder_8_out), .out(adder_9_out), .cin(adder_12_cout), .cout(adder_9_cout));
  nand nand_6 (nand_6_out, A[0], B[3]);
  Adder #(.width(1)) adder_10 (.a(nand_6_out), .b(adder_9_out), .out(\output [3]), .cin(1'b0), .cout(adder_10_cout));
  and and_5 (and_5_out, A[2], B[0]);
  and and_6 (and_6_out, B[1], A[1]);
  Adder #(.width(1)) adder_11 (
    .a(and_6_out), .b(and_5_out), .out(adder_11_out), .cin(adder_13_cout), .cout(adder_11_cout));
  and and_7 (and_7_out, A[0], B[2]);
  Adder #(.width(1)) adder_12 (.a(and_7_out), .b(adder_11_out), .out(\output [2]), .cin(1'b0), .cout(adder_12_cout));
  and and_8 (and_8_out, A[1], B[0]);
  and and_9 (and_9_out, A[0], B[1]);
  Adder #(.width(1)) adder_13 (.a(and_9_out), .b(and_8_out), .out(\output [1]), .cin(1'b0), .cout(adder_13_cout));
  and and_10 (\output [0], A[0], B[0]);
  nand nand_7 (nand_7_out, adder_7_out[6], adder_7_out[5], adder_7_out[7], adder_7_out[4], \output [3]);
  xnor xnor_1 (Overflow, nand_7_out, nand_8_out);
  nand nand_8 (nand_8_out, not_1_out, not_2_out, not_3_out, not_4_out, not_5_out);
  not not_1 (not_1_out, adder_7_out[6]);
  not not_2 (not_2_out, adder_7_out[5]);
  not not_3 (not_3_out, adder_7_out[4]);
  not not_4 (not_4_out, \output [3]);
  not not_5 (not_5_out, adder_7_out[7]);

  // Notes on the sheet:
  //   A3
  //   A2
  //   P7
  //   P6
  //   A3
  //   A2
  //   A1
  //   P5
  //   A2
  //   A1
  //   A0
  //   P4
  //   A
  //   A1
  //   A0
  //   P3
  //   P2
  //   P1
  //   A0
  //   B3
  //   P0
  //   B
  //   B0
  //   B1
  //   B2
  //   B0
  //   overflow
  //   8 bit output
endmodule
